# Fritzing sketch placa (saved by Fritzing 0.9.3b)
breadboards: 2

parts:
  WeMos_D1_Mini1 = WeMos D1 Mini  # not connected
  S1 = Pushbutton [package="[THT]"]
  U1 = LIPO-110mAh [package=lipo-110]
  R1 = Resistor [tolerance=±5% resistance=100 package="0603 [SMD]"]
  R3 = Resistor [tolerance=±5% resistance=1k package=THT]
  R4 = Resistor [tolerance=±5% resistance=47k package="0603 [SMD]"]
  R5 = Resistor [tolerance=±5% resistance=10k package="0603 [SMD]"]
  R6 = Resistor [tolerance=±5% resistance=2.2k package="0603 [SMD]"]  # not connected
  TP1 = TP4056 [chip_label=TP4056 package="DIP (Dual Inline) [THT]"]

nets:
  N1: S1.Pin_1, S1.Pin_2, R1.Pin_1, R4.Pin_1, TP1.pin6
  N2: S1.Pin_3, S1.Pin_4, R3.Pin_0
  N3: U1.+, TP1.pin4
  N4: U1.-, TP1.pin5
  N5: R1.Pin_0, R5.Pin_1, TP1.pin3

custom parts:
  TP4056: A DIP stand-in part for whatever IC you want. With 6 pins on a 300mil dual inline package (DIP) footprint.
